// Logisim project datapath.circ as structural Verilog: 8 circuits, main circuit main
module main (
);

  wire ALUSrc, and_1_out, Branch, clk, I, JBit, JC, MemRead, MemToReg, MemWrite, not_1_out, not_2_out,
       or_1_out, R, RegDst, RegWrite, Reset_out, Zero;
  wire [1:0] ALUOp;
  wire [3:0] ADD0, ADD1, ADD2, ADD3, DataRD0, DataRD1, DataRD2, DataRD3, DataRD4, DataRD5, DataRD6, DataRD7,
       DataRS0, DataRS1, DataRS2, DataRS3, DataRS4, DataRS5, DataRS6, DataRS7, DataRT0, DataRT1, DataRT2,
       DataRT3, DataRT4, DataRT5, DataRT6, DataRT7, J0, J1, J2, J3, J4, J5, J6, Operation, RD0, RD1, RS0,
       RS1, RT0, RT1;
  wire [4:0] multiplexer_2_out, RD, RS, RT;
  wire [5:0] FUNCT, OPCODE;
  wire [6:0] D0, D1, D2, D3;
  wire [15:0] ADDRESS;
  wire [23:0] bit_extender_2_out, bit_extender_4_out;
  wire [25:0] J, J_Address;
  wire [25:24] controlled_buffer_5_out;
  wire [27:0] bit_extender_1_out, PC;
  wire [31:0] adder_2_out, controlled_buffer_1_out, DataRS, DataRT, Immd, J_Shifted, multiplexer_4_out,
       multiplexer_6_out, PCDIr, PCResult, register_1_q, Res, Result, rom_1_data;

  Button button_1 (.out(clk));
  Register #(.width(32)) register_1 (.D(PCDIr), .Q(register_1_q), .clk(clk), .clr(Reset_out));  // open: en
  Button Reset (.out(Reset_out));
  assign bit_extender_1_out = {{2{1'b0}}, J_Address};  // Bit_Extender bit_extender_1
  Hex_Digit_Display hex_digit_display_1 (.value(J0));  // open: dp
  Hex_Digit_Display hex_digit_display_2 (.value(J1));  // open: dp
  Hex_Digit_Display hex_digit_display_3 (.value(DataRS0));  // open: dp
  Hex_Digit_Display hex_digit_display_4 (.value(DataRS1));  // open: dp
  Multiplexer #(.width(32), .enable("false")) multiplexer_1 (.in0(PCResult), .in1(J_Shifted), .out(PCDIr), .sel(JBit));
  Adder #(.width(32)) adder_1 (.a(register_1_q), .b(32'h1), .out({J_Shifted[31:28], PC}));  // open: cin, cout
  Bit_Extender #(.in_width(32), .out_width(24)) bit_extender_2 (.in(register_1_q), .out(bit_extender_2_out));
  Shifter #(.width(28)) shifter_1 (.in(bit_extender_1_out), .\dist (5'b00010), .out(J_Shifted[27:0]));
  display display_1 (
    .OPCODE(OPCODE), .ALUSrc(ALUSrc), .RS(RS), .RT(RT), .RD(RD), .FUNCT(FUNCT), .ADDRESS(ADDRESS),
    .Result(Result), .JC(JC), .D0(D0), .D1(D1), .D2(D2), .D3(D3), .J(J), .RS0(RS0), .RS1(RS1), .RT0(RT0),
    .RT1(RT1), .ADD0(ADD0), .ADD1(ADD1), .ADD2(ADD2), .ADD3(ADD3), .RD0(RD0), .RD1(RD1), .out_25(R),
    .out_26(I));
  Hex_Digit_Display hex_digit_display_5 (.value(J3));  // open: dp
  Hex_Digit_Display hex_digit_display_6 (.value(J2));  // open: dp
  Hex_Digit_Display hex_digit_display_7 (.value(DataRS2));  // open: dp
  Hex_Digit_Display hex_digit_display_8 (.value(DataRS3));  // open: dp
  Hex_Digit_Display hex_digit_display_9 (.value(J4));  // open: dp
  Hex_Digit_Display hex_digit_display_10 (.value(J5));  // open: dp
  Hex_Digit_Display hex_digit_display_11 (.value(DataRS5));  // open: dp
  Hex_Digit_Display hex_digit_display_12 (.value(DataRS4));  // open: dp
  ROM #(.addrWidth(24), .dataWidth(32)) rom_1 (.addr(bit_extender_2_out), .data(rom_1_data));  // open: sel
  decoder decoder (
    .in_1(rom_1_data), .ADDRESS(ADDRESS), .RT(RT), .RS(RS), .OPCODE(OPCODE), .RD(RD), .FUNCT(FUNCT),
    .J_Address(J_Address));
  Hex_Digit_Display hex_digit_display_13 (.value(J6));  // open: dp
  Hex_Digit_Display hex_digit_display_14 (.value(DataRS6));  // open: dp
  Hex_Digit_Display hex_digit_display_15 (.value(DataRS7));  // open: dp
  Control control_1 (
    .OPCODE(OPCODE), .RegDst(RegDst), .Branch(Branch), .MemRead(MemRead), .MemToReg(MemToReg), .ALUOp(ALUOp),
    .J(JBit), .MemWrite(MemWrite), .ALUSrc(ALUSrc), .RegWrite(RegWrite));
  Hex_Digit_Display hex_digit_display_16 (.value(DataRT0));  // open: dp
  Hex_Digit_Display hex_digit_display_17 (.value(DataRT1));  // open: dp
  Adder #(.width(32)) adder_2 (.a({J_Shifted[31:28], PC}), .b(Immd), .out(adder_2_out));  // open: cin, cout
  and and_1 (and_1_out, Zero, Branch);
  Multiplexer #(.width(5), .enable("false")) multiplexer_2 (.in0(RT), .in1(RD), .out(multiplexer_2_out), .sel(RegDst));
  Hex_Digit_Display hex_digit_display_18 (.value(ADD1));  // open: dp
  Hex_Digit_Display hex_digit_display_19 (.value(ADD0));  // open: dp
  Hex_Digit_Display hex_digit_display_20 (.value(DataRT3));  // open: dp
  Hex_Digit_Display hex_digit_display_21 (.value(DataRT2));  // open: dp
  Multiplexer #(.width(32), .enable("false")) multiplexer_3 (
    .in0({J_Shifted[31:28], PC}), .in1(adder_2_out), .out(PCResult), .sel(and_1_out));
  Registros registros_1 (
    .RS(RS), .RT(RT), .DestReg(multiplexer_2_out), .WriteData(Res), .Clock(clk), .RegWrite(RegWrite),
    .RSData(DataRS), .RTData(DataRT));
  Hex_Digit_Display hex_digit_display_22 (.value(ADD2));  // open: dp
  Hex_Digit_Display hex_digit_display_23 (.value(ADD3));  // open: dp
  Hex_Digit_Display hex_digit_display_24 (.value(DataRT4));  // open: dp
  Hex_Digit_Display hex_digit_display_25 (.value(DataRT5));  // open: dp
  Multiplexer #(.width(32), .enable("false")) multiplexer_4 (
    .in0(DataRT), .in1(Immd), .out(multiplexer_4_out), .sel(ALUSrc));
  ALUControl ALUControl (.ALUOp(ALUOp), .FUNCT(FUNCT), .Operation(Operation));
  assign Immd = {{16{ADDRESS[15]}}, ADDRESS};  // Bit_Extender bit_extender_3
  Hex_Digit_Display hex_digit_display_26 (.value(DataRT6));  // open: dp
  Hex_Digit_Display hex_digit_display_27 (.value(DataRT7));  // open: dp
  Hex_Digit_Display hex_digit_display_28 (.value(RS0));  // open: dp
  Hex_Digit_Display hex_digit_display_29 (.value(DataRD0));  // open: dp
  ALU alu_1 (.RSData(DataRS), .RT_RDData(multiplexer_4_out), .Operation(Operation), .Zero(Zero), .Result(Result));
  assign controlled_buffer_1_out = MemWrite ? DataRT : 32'bz;  // Controlled_Buffer controlled_buffer_1
  Bit_Extender #(.in_width(32), .out_width(24)) bit_extender_4 (.in(Result), .out(bit_extender_4_out));
  _7_Segment_Display u_7_segment_display_1 (
    .g(D0[3]), .f(D0[2]), .a(D0[1]), .b(D0[0]), .e(D0[4]), .d(D0[5]), .c(D0[6]));  // open: dp
  Hex_Digit_Display hex_digit_display_30 (.value(RS1));  // open: dp
  Hex_Digit_Display hex_digit_display_31 (.value(DataRD2));  // open: dp
  Hex_Digit_Display hex_digit_display_32 (.value(DataRD1));  // open: dp
  or or_1 (or_1_out, MemWrite, MemRead);
  Hex_Digit_Display hex_digit_display_33 (.value(DataRD3));  // open: dp
  Hex_Digit_Display hex_digit_display_34 (.value(DataRD4));  // open: dp
  RAM #(.addrWidth(24), .dataWidth(32), .bus("asynch")) ram_1 (
    .addr(bit_extender_4_out), .data(controlled_buffer_1_out), .sel(or_1_out), .ld(MemRead));  // open: clr
  _7_Segment_Display u_7_segment_display_2 (
    .g(D1[3]), .f(D1[2]), .a(D1[1]), .b(D1[0]), .e(D1[4]), .d(D1[5]), .c(D1[6]));  // open: dp
  Hex_Digit_Display hex_digit_display_35 (.value(RT0));  // open: dp
  Hex_Digit_Display hex_digit_display_36 (.value(RT1));  // open: dp
  Hex_Digit_Display hex_digit_display_37 (.value(DataRD5));  // open: dp
  Hex_Digit_Display hex_digit_display_38 (.value(DataRD6));  // open: dp
  Multiplexer #(.width(32), .enable("false")) multiplexer_5 (
    .in0(Result), .in1(controlled_buffer_1_out), .out(Res), .sel(MemToReg));
  _7_Segment_Display u_7_segment_display_3 (
    .g(D2[3]), .f(D2[2]), .a(D2[1]), .b(D2[0]), .e(D2[4]), .d(D2[5]), .c(D2[6]));  // open: dp
  Hex_Digit_Display hex_digit_display_39 (.value(DataRD7));  // open: dp
  _7_Segment_Display u_7_segment_display_4 (
    .g(D3[3]), .f(D3[2]), .a(D3[1]), .b(D3[0]), .e(D3[4]), .d(D3[5]), .c(D3[6]));  // open: dp
  Hex_Digit_Display hex_digit_display_40 (.value(RD0));  // open: dp
  Hex_Digit_Display hex_digit_display_41 (.value(RD1));  // open: dp
  not not_1 (not_1_out, JC);
  Multiplexer #(.width(32), .enable("false")) multiplexer_6 (
    .in0(DataRT), .in1(Result), .out(multiplexer_6_out), .sel(I));
  not not_2 (not_2_out, JC);
  assign {DataRS0, DataRS1, DataRS2, DataRS3, DataRS4, DataRS5, DataRS6, DataRS7} = not_1_out ? DataRS : 32'bz;  // Controlled_Buffer controlled_buffer_2
  assign {DataRT0, DataRT1, DataRT2, DataRT3, DataRT4, DataRT5, DataRT6, DataRT7} = not_2_out ? multiplexer_6_out : 32'bz;  // Controlled_Buffer controlled_buffer_3
  assign {DataRD0, DataRD1, DataRD2, DataRD3, DataRD4, DataRD5, DataRD6, DataRD7} = R ? Result : 32'bz;  // Controlled_Buffer controlled_buffer_4
  assign {controlled_buffer_5_out, J1, J2, J3, J4, J5, J6} = JC ? J : 26'bz;  // Controlled_Buffer controlled_buffer_5
  assign J0 = {{2{1'b0}}, controlled_buffer_5_out};  // Bit_Extender bit_extender_5

  // Other names for the same wires on the sheet: PC[31:28] = J_Shifted[31:28]

  // Notes on the sheet:
  //   JUMP ADDRESS
  //   RS Data
  //   contents of rom_1 (hex, n*v repeats v):
  //   80009c4 80009c4
  //   IMMD/ADDRESS
  //   RT Data
  //   RS
  //   RD Data
  //   INSTRUCTION
  //   RT
  //   RD
endmodule

module decoder (
  input  [31:0] in_1,
  output [5:0] FUNCT,
  output [4:0] RD,
  output [15:0] ADDRESS,
  output [4:0] RT,
  output [4:0] RS,
  output [5:0] OPCODE,
  output [25:0] J_Address
);


  assign ADDRESS = in_1[15:0];
  assign FUNCT = in_1[5:0];
  assign J_Address = in_1[25:0];
  assign OPCODE = in_1[31:26];
  assign RD = in_1[15:11];
  assign RS = in_1[25:21];
  assign RT = in_1[20:16];
endmodule

module test (
  input  [4:0] in_1,
  input  [2:0] in_2,
  input  [31:0] in_3,
  output [4:0] out_4,
  output [4:0] out_5,
  output [4:0] out_6,
  output [4:0] out_7,
  output [4:0] out_8,
  output [4:0] out_9,
  output [4:0] out_10,
  output [4:0] out_11
);

  wire multiplexer_1_out;

  Demultiplexer #(.select(3), .width(5), .tristate("true"), .enable("false")) demultiplexer_1 (
    .out0(out_4), .out1(out_5), .out2(out_6), .out3(out_7), .out4(out_8), .out5(out_9), .out6(out_10),
    .out7(out_11), .in(in_1), .sel(in_2));
  RAM #(.dataWidth(32)) ram_1 ();  // open: addr, data, sel, clk, ld, clr
  Multiplexer #(.enable("false")) multiplexer_1 (.in0(1'b0), .in1(1'b1), .out(multiplexer_1_out));  // open: sel
  // Probe on multiplexer_1_out
endmodule

module Control (
  input  [5:0] OPCODE,
  output RegDst,
  output Branch,
  output MemRead,
  output MemToReg,
  output [1:0] ALUOp,
  output J,
  output MemWrite,
  output ALUSrc,
  output RegWrite
);

  wire addi, beq, lw, multiplexer_1_out, multiplexer_4_out, not_1_out, not_2_out, not_3_out, or_1_out,
       or_2_out, or_3_out, or_4_out, or_5_out, R, sw;
  wire [1:0] multiplexer_8_out, multiplexer_9_out, multiplexer_10_out;

  Multiplexer #(.enable("false")) multiplexer_1 (.in0(1'b0), .in1(1'b1), .out(multiplexer_1_out), .sel(R));
  Multiplexer #(.enable("false")) multiplexer_2 (.in0(1'b0), .in1(1'b1), .out(Branch), .sel(beq));
  Multiplexer #(.enable("false")) multiplexer_3 (.in0(1'b0), .in1(1'b1), .out(MemRead), .sel(lw));
  Multiplexer #(.enable("false")) multiplexer_4 (.in0(1'b0), .in1(1'b1), .out(multiplexer_4_out), .sel(lw));
  Multiplexer #(.enable("false")) multiplexer_5 (.in0(1'b0), .in1(1'b1), .out(MemWrite), .sel(sw));
  Multiplexer #(.enable("false")) multiplexer_6 (.in0(1'b0), .in1(1'b1), .out(ALUSrc), .sel(or_1_out));
  or or_1 (or_1_out, lw, sw, not_1_out);
  Multiplexer #(.enable("false")) multiplexer_7 (.in0(1'b0), .in1(1'b1), .out(RegWrite), .sel(or_2_out));
  or or_2 (or_2_out, lw, addi, R);
  or or_3 (or_3_out, sw, beq);
  or or_4 (or_4_out, sw, beq);
  not not_1 (not_1_out, R);
  assign RegDst = not_2_out ? multiplexer_1_out : 1'bz;  // Controlled_Buffer controlled_buffer_1
  not not_2 (not_2_out, or_3_out);
  assign MemToReg = not_3_out ? multiplexer_4_out : 1'bz;  // Controlled_Buffer controlled_buffer_2
  not not_3 (not_3_out, or_4_out);
  Comparator #(.width(6)) comparator_1 (.a(OPCODE), .b(6'b100011), .eq(lw));  // open: gt, lt
  Comparator #(.width(6)) comparator_2 (.a(OPCODE), .b(6'b101011), .eq(sw));  // open: gt, lt
  Comparator #(.width(6)) comparator_3 (.a(OPCODE), .b(6'b001000), .eq(addi));  // open: gt, lt
  Comparator #(.width(6)) comparator_4 (.a(OPCODE), .b({6{1'b0}}), .eq(R));  // open: gt, lt
  Comparator #(.width(6)) comparator_5 (.a(OPCODE), .b(6'b000100), .eq(beq));  // open: gt, lt
  Comparator #(.width(6)) comparator_6 (.a(OPCODE), .b(6'b000010), .eq(J));  // open: gt, lt
  or or_5 (or_5_out, lw, sw, addi);
  Multiplexer #(.width(2), .enable("false")) multiplexer_8 (
    .in0(2'b00), .in1(2'b00), .out(multiplexer_8_out), .sel(or_5_out));
  Multiplexer #(.width(2), .enable("false")) multiplexer_9 (.in0(2'b00), .in1(2'b10), .out(multiplexer_9_out), .sel(R));
  assign ALUOp = multiplexer_8_out | multiplexer_9_out | multiplexer_10_out;  // OR_Gate or_6, 2 bits wide
  Multiplexer #(.width(2), .enable("false")) multiplexer_10 (
    .in0(2'b00), .in1(2'b01), .out(multiplexer_10_out), .sel(beq));

  // Notes on the sheet:
  //   lw
  //   sw
  //   R-type
  //   beq
endmodule

module ALUControl (
  input  [1:0] ALUOp,
  input  [5:0] FUNCT,
  output [3:0] Operation
);

  wire add2, and_3_out, and_4_out, and_5_out, beq_sub1, comparator_1_eq, comparator_2_eq, comparator_3_eq,
       comparator_4_eq, comparator_5_eq, lw_sw_add1, or_1_out, or_2_out, R, sub2;
  wire [3:0] add, \and , mult, \or , sub;

  Comparator #(.width(6)) comparator_1 (.a(FUNCT), .b(6'b100000), .eq(comparator_1_eq));  // open: gt, lt
  Comparator #(.width(6)) comparator_2 (.a(FUNCT), .b(6'b100010), .eq(comparator_2_eq));  // open: gt, lt
  Comparator #(.width(6)) comparator_3 (.a(FUNCT), .b(6'b100100), .eq(comparator_3_eq));  // open: gt, lt
  Comparator #(.width(6)) comparator_4 (.a(FUNCT), .b(6'b100101), .eq(comparator_4_eq));  // open: gt, lt
  Comparator #(.width(6)) comparator_5 (.a(FUNCT), .b(6'b011000), .eq(comparator_5_eq));  // open: gt, lt
  or or_1 (or_1_out, lw_sw_add1, add2);
  or or_2 (or_2_out, beq_sub1, sub2);
  and and_1 (add2, comparator_1_eq, R);
  and and_2 (sub2, comparator_2_eq, R);
  and and_3 (and_3_out, comparator_3_eq, R);
  and and_4 (and_4_out, comparator_4_eq, R);
  and and_5 (and_5_out, comparator_5_eq, R);
  Comparator #(.width(2)) comparator_6 (.a(ALUOp), .b(2'b00), .eq(lw_sw_add1));  // open: gt, lt
  Comparator #(.width(1)) comparator_7 (.a(ALUOp[0]), .b(1'b1), .eq(beq_sub1));  // open: gt, lt
  Comparator #(.width(1)) comparator_8 (.a(ALUOp[1]), .b(1'b1), .eq(R));  // open: gt, lt
  Multiplexer #(.width(4), .enable("false")) multiplexer_1 (.in0(4'b0000), .in1(4'b0010), .out(add), .sel(or_1_out));
  Multiplexer #(.width(4), .enable("false")) multiplexer_2 (.in0(4'b0000), .in1(4'b0110), .out(sub), .sel(or_2_out));
  Multiplexer #(.width(4), .enable("false")) multiplexer_3 (.in0(4'b0000), .in1(4'b0000), .out(\and ), .sel(and_3_out));
  Multiplexer #(.width(4), .enable("false")) multiplexer_4 (.in0(4'b0000), .in1(4'b0001), .out(\or ), .sel(and_4_out));
  Multiplexer #(.width(4), .enable("false")) multiplexer_5 (.in0(4'b0000), .in1(4'b0101), .out(mult), .sel(and_5_out));
  assign Operation = add | sub | \and  | \or  | mult;  // OR_Gate or_3, 4 bits wide
endmodule

module ALU (
  input  [31:0] RSData,
  input  [31:0] RT_RDData,
  input  [3:0] Operation,
  output Zero,
  output [31:0] Result
);

  wire [31:0] adder_1_out, and_1_out, multiplier_1_out, or_1_out, subtractor_1_out;

  assign and_1_out = RSData & RT_RDData;  // AND_Gate and_1, 32 bits wide
  assign or_1_out = RSData | RT_RDData;  // OR_Gate or_1, 32 bits wide
  Adder #(.width(32)) adder_1 (.a(RSData), .b(RT_RDData), .out(adder_1_out));  // open: cin, cout
  Multiplier #(.width(32)) multiplier_1 (.a(RSData), .b(RT_RDData), .out(multiplier_1_out));  // open: cin, cout
  Subtractor #(.width(32)) subtractor_1 (.a(RSData), .b(RT_RDData), .out(subtractor_1_out));  // open: bin, bout
  Multiplexer #(.select(4), .width(32), .enable("false")) multiplexer_1 (
    .in0(and_1_out), .in1(or_1_out), .in2(adder_1_out), .in5(multiplier_1_out), .in6(subtractor_1_out),
    .out(Result), .sel(Operation));  // open: in3, in4, in7, in8, in9, in10, in11, in12, in13, in14, in15
  Comparator #(.width(32)) comparator_1 (.a({32{1'b0}}), .b(Result), .eq(Zero));  // open: gt, lt
endmodule

module Registros (
  input  RegWrite,
  input  [4:0] RS,
  input  [4:0] RT,
  input  [4:0] DestReg,
  input  [31:0] WriteData,
  input  Clock,
  output [31:0] RSData,
  output [31:0] RTData
);

  wire [31:0] R0, R1, R2, R3, R4, R5, R6, R7, R8, R9, R10, R11, R12, R13, R14, R15, R16, R17, R18, R19, R20,
       R21, R22, R23, R24, R25, R26, R27, R28, R29, R30, R31, Reg0, Reg1, Reg2, Reg3, Reg4, Reg5, Reg6, Reg7,
       Reg8, Reg9, Reg10, Reg11, Reg12, Reg13, Reg14, Reg15, Reg16, Reg17, Reg18, Reg19, Reg20, Reg21, Reg22,
       Reg23, Reg24, Reg25, Reg26, Reg27, Reg28, Reg29, Reg30, Reg31;

  Demultiplexer #(.select(5), .width(32), .tristate("true"), .enable("false")) demultiplexer_1 (
    .out0(Reg0), .out1(Reg1), .out2(Reg2), .out3(Reg3), .out4(Reg4), .out5(Reg5), .out6(Reg6), .out7(Reg7),
    .out8(Reg8), .out9(Reg9), .out10(Reg10), .out11(Reg11), .out12(Reg12), .out13(Reg13), .out14(Reg14),
    .out15(Reg15), .out16(Reg16), .out17(Reg17), .out18(Reg18), .out19(Reg19), .out20(Reg20), .out21(Reg21),
    .out22(Reg22), .out23(Reg23), .out24(Reg24), .out25(Reg25), .out26(Reg26), .out27(Reg27), .out28(Reg28),
    .out29(Reg29), .out30(Reg30), .out31(Reg31), .in(WriteData), .sel(DestReg));
  Register #(.width(32)) _00000 (.D(Reg0), .en(RegWrite), .Q(R0), .clk(Clock));  // open: clr
  Register #(.width(32)) _00001 (.D(Reg1), .en(RegWrite), .Q(R1), .clk(Clock));  // open: clr
  Register #(.width(32)) _00010 (.D(Reg2), .en(RegWrite), .Q(R2), .clk(Clock));  // open: clr
  Register #(.width(32)) _00011 (.D(Reg3), .en(RegWrite), .Q(R3), .clk(Clock));  // open: clr
  Register #(.width(32)) _00100 (.D(Reg4), .en(RegWrite), .Q(R4), .clk(Clock));  // open: clr
  Register #(.width(32)) _00101 (.D(Reg5), .en(RegWrite), .Q(R5), .clk(Clock));  // open: clr
  Register #(.width(32)) _00110 (.D(Reg6), .en(RegWrite), .Q(R6), .clk(Clock));  // open: clr
  Register #(.width(32)) _00111 (.D(Reg7), .en(RegWrite), .Q(R7), .clk(Clock));  // open: clr
  Register #(.width(32)) _01000 (.D(Reg8), .en(RegWrite), .Q(R8), .clk(Clock));  // open: clr
  Register #(.width(32)) _01001 (.D(Reg9), .en(RegWrite), .Q(R9), .clk(Clock));  // open: clr
  Register #(.width(32)) _01010 (.D(Reg10), .en(RegWrite), .Q(R10), .clk(Clock));  // open: clr
  Register #(.width(32)) _01011 (.D(Reg11), .en(RegWrite), .Q(R11), .clk(Clock));  // open: clr
  Register #(.width(32)) _01100 (.D(Reg12), .en(RegWrite), .Q(R12), .clk(Clock));  // open: clr
  Register #(.width(32)) _01101 (.D(Reg13), .en(RegWrite), .Q(R13), .clk(Clock));  // open: clr
  Register #(.width(32)) _01110 (.D(Reg14), .en(RegWrite), .Q(R14), .clk(Clock));  // open: clr
  Register #(.width(32)) _01111 (.D(Reg15), .en(RegWrite), .Q(R15), .clk(Clock));  // open: clr
  Register #(.width(32)) _10000 (.D(Reg16), .en(RegWrite), .Q(R16), .clk(Clock));  // open: clr
  Register #(.width(32)) _10001 (.D(Reg17), .en(RegWrite), .Q(R17), .clk(Clock));  // open: clr
  Register #(.width(32)) _10010 (.D(Reg18), .en(RegWrite), .Q(R18), .clk(Clock));  // open: clr
  Register #(.width(32)) _10011 (.D(Reg19), .en(RegWrite), .Q(R19), .clk(Clock));  // open: clr
  Register #(.width(32)) _10100 (.D(Reg20), .en(RegWrite), .Q(R20), .clk(Clock));  // open: clr
  Register #(.width(32)) _10101 (.D(Reg21), .en(RegWrite), .Q(R21), .clk(Clock));  // open: clr
  Register #(.width(32)) _10110 (.D(Reg22), .en(RegWrite), .Q(R22), .clk(Clock));  // open: clr
  Register #(.width(32)) _10111 (.D(Reg23), .en(RegWrite), .Q(R23), .clk(Clock));  // open: clr
  Register #(.width(32)) _11000 (.D(Reg24), .en(RegWrite), .Q(R24), .clk(Clock));  // open: clr
  Register #(.width(32)) _11001 (.D(Reg25), .en(RegWrite), .Q(R25), .clk(Clock));  // open: clr
  Register #(.width(32)) _11010 (.D(Reg26), .en(RegWrite), .Q(R26), .clk(Clock));  // open: clr
  Register #(.width(32)) _11011 (.D(Reg27), .en(RegWrite), .Q(R27), .clk(Clock));  // open: clr
  Register #(.width(32)) _11100 (.D(Reg28), .en(RegWrite), .Q(R28), .clk(Clock));  // open: clr
  Register #(.width(32)) _11101 (.D(Reg29), .en(RegWrite), .Q(R29), .clk(Clock));  // open: clr
  Register #(.width(32)) _11110 (.D(Reg30), .en(RegWrite), .Q(R30), .clk(Clock));  // open: clr
  Register #(.width(32)) _11111 (.D(Reg31), .en(RegWrite), .Q(R31), .clk(Clock));  // open: clr
  Multiplexer #(.select(5), .width(32), .enable("false")) multiplexer_1 (
    .in0(R0), .in1(R1), .in2(R2), .in3(R3), .in4(R4), .in5(R5), .in6(R6), .in7(R7), .in8(R8), .in9(R9),
    .in10(R10), .in11(R11), .in12(R12), .in13(R13), .in14(R14), .in15(R15), .in16(R16), .in17(R17),
    .in18(R18), .in19(R19), .in20(R20), .in21(R21), .in22(R22), .in23(R23), .in24(R24), .in25(R25),
    .in26(R26), .in27(R27), .in28(R28), .in29(R29), .in30(R20), .in31(R31), .out(RSData), .sel(RS));
  Multiplexer #(.select(5), .width(32), .enable("false")) multiplexer_2 (
    .in0(R0), .in1(R1), .in2(R2), .in3(R3), .in4(R4), .in5(R5), .in6(R6), .in7(R7), .in8(R8), .in9(R9),
    .in10(R10), .in11(R11), .in12(R12), .in13(R13), .in14(R14), .in15(R15), .in16(R16), .in17(R17),
    .in18(R18), .in19(R19), .in20(R20), .in21(R21), .in22(R22), .in23(R23), .in24(R24), .in25(R25),
    .in26(R26), .in27(R27), .in28(R28), .in29(R29), .in30(R20), .in31(R31), .out(RTData), .sel(RT));
endmodule

module display (
  input  [5:0] OPCODE,
  input  ALUSrc,
  input  [4:0] RS,
  input  [4:0] RT,
  input  [4:0] RD,
  input  [5:0] FUNCT,
  input  [15:0] ADDRESS,
  input  [31:0] Result,
  output JC,
  output [6:0] D0,
  output [6:0] D1,
  output [6:0] D2,
  output [6:0] D3,
  output [25:0] J,
  output [3:0] RS0,
  output [3:0] RS1,
  output [3:0] RT0,
  output [3:0] RT1,
  output [3:0] ADD0,
  output [3:0] ADD1,
  output [3:0] ADD2,
  output [3:0] ADD3,
  output [3:0] RD0,
  output [3:0] RD1,
  output out_25,
  output out_26
);

  wire add, addi, \and , beq, comparator_8_eq, comparator_9_eq, comparator_10_eq, comparator_11_eq,
       comparator_12_eq, comparator_13_eq, I1, I2, I4, mult, \nor , \or , or_2_out, sub;
  wire [4:4] multiplexer_1_out, multiplexer_2_out, multiplexer_4_out;
  wire [6:0] multiplexer_5_out, multiplexer_6_out, multiplexer_7_out, multiplexer_8_out, multiplexer_9_out,
       multiplexer_10_out, multiplexer_11_out, multiplexer_12_out, multiplexer_13_out, multiplexer_14_out,
       multiplexer_15_out, multiplexer_16_out, multiplexer_17_out, multiplexer_18_out, multiplexer_19_out,
       multiplexer_20_out, multiplexer_21_out, multiplexer_22_out, multiplexer_23_out, multiplexer_24_out,
       multiplexer_25_out, multiplexer_26_out, multiplexer_27_out, multiplexer_28_out, multiplexer_29_out,
       multiplexer_30_out, multiplexer_31_out, multiplexer_32_out, multiplexer_33_out, multiplexer_34_out,
       multiplexer_35_out, multiplexer_36_out, multiplexer_37_out, multiplexer_38_out, multiplexer_39_out,
       multiplexer_40_out, multiplexer_41_out, multiplexer_42_out, multiplexer_43_out, multiplexer_44_out,
       multiplexer_45_out, multiplexer_46_out, multiplexer_47_out, multiplexer_48_out, multiplexer_49_out,
       multiplexer_50_out, multiplexer_51_out, multiplexer_52_out;

  or or_1 (out_26, I1, I2, addi, I4, beq);
  Multiplexer #(.width(5), .enable("false")) multiplexer_1 (
    .in0(RS), .out({multiplexer_1_out[4], RS1}), .sel(JC));  // open: in1
  Multiplexer #(.width(5), .enable("false")) multiplexer_2 (
    .in0(RT), .out({multiplexer_2_out[4], RT1}), .sel(JC));  // open: in1
  Comparator #(.width(6)) comparator_1 (.a(OPCODE), .b({6{1'b0}}), .eq(out_25));  // open: gt, lt
  Comparator #(.width(6)) comparator_2 (.a(OPCODE), .b(6'b100011), .eq(I1));  // open: gt, lt
  Comparator #(.width(6)) comparator_3 (.a(OPCODE), .b(6'b101011), .eq(I2));  // open: gt, lt
  Comparator #(.width(6)) comparator_4 (.a(OPCODE), .b(6'b001000), .eq(addi));  // open: gt, lt
  Comparator #(.width(6)) comparator_5 (.a(OPCODE), .b(6'b001101), .eq(I4));  // open: gt, lt
  Comparator #(.width(6)) comparator_6 (.a(OPCODE), .b(6'b000100), .eq(beq));  // open: gt, lt
  Comparator #(.width(6)) comparator_7 (.a(OPCODE), .b(6'b000010), .eq(JC));  // open: gt, lt
  Comparator #(.width(6)) comparator_8 (.a(FUNCT), .b(6'b100000), .eq(comparator_8_eq));  // open: gt, lt
  and and_1 (add, comparator_8_eq, out_25);
  and and_2 (sub, comparator_9_eq, out_25);
  Comparator #(.width(6)) comparator_9 (.a(FUNCT), .b(6'b100010), .eq(comparator_9_eq));  // open: gt, lt
  Comparator #(.width(6)) comparator_10 (.a(FUNCT), .b(6'b100100), .eq(comparator_10_eq));  // open: gt, lt
  and and_3 (\and , comparator_10_eq, out_25);
  Comparator #(.width(6)) comparator_11 (.a(FUNCT), .b(6'b100101), .eq(comparator_11_eq));  // open: gt, lt
  and and_4 (\or , comparator_11_eq, out_25);
  and and_5 (\nor , comparator_12_eq, out_25);
  Comparator #(.width(6)) comparator_12 (.a(FUNCT), .b(6'b100111), .eq(comparator_12_eq));  // open: gt, lt
  Comparator #(.width(6)) comparator_13 (.a(FUNCT), .b(6'b011000), .eq(comparator_13_eq));  // open: gt, lt
  and and_6 (mult, comparator_13_eq, out_25);
  assign RS0 = {{3{1'b0}}, multiplexer_1_out[4]};  // Bit_Extender bit_extender_1
  assign RT0 = {{3{1'b0}}, multiplexer_2_out[4]};  // Bit_Extender bit_extender_2
  Multiplexer #(.width(16), .enable("false")) multiplexer_3 (
    .in1(ADDRESS), .out({ADD0, ADD1, ADD2, ADD3}), .sel(out_26));  // open: in0
  Multiplexer #(.width(5), .enable("false")) multiplexer_4 (
    .in0(ADDRESS[15:11]), .out({multiplexer_4_out[4], RD1}), .sel(or_2_out));  // open: in1
  or or_2 (or_2_out, out_26, JC);
  assign RD0 = {{3{1'b0}}, multiplexer_4_out[4]};  // Bit_Extender bit_extender_3
  Multiplexer #(.width(7), .enable("false")) multiplexer_5 (
    .in0({7{1'b0}}), .in1({7{1'b0}}), .out(multiplexer_5_out), .sel(add));
  Multiplexer #(.width(7), .enable("false")) multiplexer_6 (
    .in0({7{1'b0}}), .in1({7{1'b0}}), .out(multiplexer_6_out), .sel(sub));
  Multiplexer #(.width(7), .enable("false")) multiplexer_7 (
    .in0({7{1'b0}}), .in1({7{1'b0}}), .out(multiplexer_7_out), .sel(\and ));
  Multiplexer #(.width(7), .enable("false")) multiplexer_8 (
    .in0({7{1'b0}}), .in1({7{1'b0}}), .out(multiplexer_8_out), .sel(\or ));
  Multiplexer #(.width(7), .enable("false")) multiplexer_9 (
    .in0({7{1'b0}}), .in1({7{1'b0}}), .out(multiplexer_9_out), .sel(\nor ));
  Multiplexer #(.width(7), .enable("false")) multiplexer_10 (
    .in0({7{1'b0}}), .in1(7'b0110100), .out(multiplexer_10_out), .sel(I1));
  Multiplexer #(.width(7), .enable("false")) multiplexer_11 (
    .in0({7{1'b0}}), .in1({7{1'b0}}), .out(multiplexer_11_out), .sel(I2));
  Multiplexer #(.width(7), .enable("false")) multiplexer_12 (
    .in0({7{1'b0}}), .in1(7'b1011111), .out(multiplexer_12_out), .sel(addi));
  Multiplexer #(.width(7), .enable("false")) multiplexer_13 (
    .in0({7{1'b0}}), .in1({7{1'b0}}), .out(multiplexer_13_out), .sel(I4));
  Multiplexer #(.width(7), .enable("false")) multiplexer_14 (
    .in0({7{1'b0}}), .in1({7{1'b0}}), .out(multiplexer_14_out), .sel(beq));
  Multiplexer #(.width(7), .enable("false")) multiplexer_15 (
    .in0({7{1'b0}}), .in1(7'b1011010), .out(multiplexer_15_out), .sel(mult));
  Multiplexer #(.width(7), .enable("false")) multiplexer_16 (
    .in0({7{1'b0}}), .in1({7{1'b0}}), .out(multiplexer_16_out), .sel(JC));
  assign D0 = multiplexer_5_out | multiplexer_6_out | multiplexer_7_out | multiplexer_8_out | multiplexer_9_out | multiplexer_10_out | multiplexer_11_out | multiplexer_12_out | multiplexer_13_out | multiplexer_14_out | multiplexer_15_out | multiplexer_16_out;  // OR_Gate or_3, 7 bits wide
  Multiplexer #(.width(7), .enable("false")) multiplexer_17 (
    .in0({7{1'b0}}), .in1(7'b1011111), .out(multiplexer_17_out), .sel(add));
  Multiplexer #(.width(7), .enable("false")) multiplexer_18 (
    .in0({7{1'b0}}), .in1(7'b1101110), .out(multiplexer_18_out), .sel(sub));
  Multiplexer #(.width(7), .enable("false")) multiplexer_19 (
    .in0({7{1'b0}}), .in1(7'b1011111), .out(multiplexer_19_out), .sel(\and ));
  Multiplexer #(.width(7), .enable("false")) multiplexer_20 (
    .in0({7{1'b0}}), .in1({7{1'b0}}), .out(multiplexer_20_out), .sel(\or ));
  Multiplexer #(.width(7), .enable("false")) multiplexer_21 (
    .in0({7{1'b0}}), .in1(7'b1011000), .out(multiplexer_21_out), .sel(\nor ));
  Multiplexer #(.width(7), .enable("false")) multiplexer_22 (
    .in0({7{1'b0}}), .in1(7'b1110111), .out(multiplexer_22_out), .sel(I1));
  Multiplexer #(.width(7), .enable("false")) multiplexer_23 (
    .in0({7{1'b0}}), .in1({7{1'b0}}), .out(multiplexer_23_out), .sel(I2));
  Multiplexer #(.width(7), .enable("false")) multiplexer_24 (
    .in0({7{1'b0}}), .in1(7'b1111001), .out(multiplexer_24_out), .sel(addi));
  Multiplexer #(.width(7), .enable("false")) multiplexer_25 (
    .in0({7{1'b0}}), .in1(7'b1110111), .out(multiplexer_25_out), .sel(I4));
  Multiplexer #(.width(7), .enable("false")) multiplexer_26 (
    .in0({7{1'b0}}), .in1(7'b1111100), .out(multiplexer_26_out), .sel(beq));
  Multiplexer #(.width(7), .enable("false")) multiplexer_27 (
    .in0({7{1'b0}}), .in1(7'b1110101), .out(multiplexer_27_out), .sel(mult));
  Multiplexer #(.width(7), .enable("false")) multiplexer_28 (
    .in0({7{1'b0}}), .in1({7{1'b0}}), .out(multiplexer_28_out), .sel(JC));
  assign D1 = multiplexer_17_out | multiplexer_18_out | multiplexer_19_out | multiplexer_20_out | multiplexer_21_out | multiplexer_22_out | multiplexer_23_out | multiplexer_24_out | multiplexer_25_out | multiplexer_26_out | multiplexer_27_out | multiplexer_28_out;  // OR_Gate or_4, 7 bits wide
  Multiplexer #(.width(7), .enable("false")) multiplexer_29 (
    .in0({7{1'b0}}), .in1(7'b1111001), .out(multiplexer_29_out), .sel(add));
  Multiplexer #(.width(7), .enable("false")) multiplexer_30 (
    .in0({7{1'b0}}), .in1(7'b1110101), .out(multiplexer_30_out), .sel(sub));
  Multiplexer #(.width(7), .enable("false")) multiplexer_31 (
    .in0({7{1'b0}}), .in1(7'b1011000), .out(multiplexer_31_out), .sel(\and ));
  Multiplexer #(.width(7), .enable("false")) multiplexer_32 (
    .in0({7{1'b0}}), .in1(7'b1110111), .out(multiplexer_32_out), .sel(\or ));
  Multiplexer #(.width(7), .enable("false")) multiplexer_33 (
    .in0({7{1'b0}}), .in1(7'b1110111), .out(multiplexer_33_out), .sel(\nor ));
  Multiplexer #(.width(7), .enable("false")) multiplexer_34 (
    .in0({7{1'b0}}), .in1(7'b1011111), .out(multiplexer_34_out), .sel(I1));
  Multiplexer #(.width(7), .enable("false")) multiplexer_35 (
    .in0({7{1'b0}}), .in1(7'b1101110), .out(multiplexer_35_out), .sel(I2));
  Multiplexer #(.width(7), .enable("false")) multiplexer_36 (
    .in0({7{1'b0}}), .in1(7'b1111001), .out(multiplexer_36_out), .sel(addi));
  Multiplexer #(.width(7), .enable("false")) multiplexer_37 (
    .in0({7{1'b0}}), .in1(7'b0011000), .out(multiplexer_37_out), .sel(I4));
  Multiplexer #(.width(7), .enable("false")) multiplexer_38 (
    .in0({7{1'b0}}), .in1(7'b0111111), .out(multiplexer_38_out), .sel(beq));
  Multiplexer #(.width(7), .enable("false")) multiplexer_39 (
    .in0({7{1'b0}}), .in1(7'b0110100), .out(multiplexer_39_out), .sel(mult));
  Multiplexer #(.width(7), .enable("false")) multiplexer_40 (
    .in0({7{1'b0}}), .in1({7{1'b0}}), .out(multiplexer_40_out), .sel(JC));
  assign D2 = multiplexer_29_out | multiplexer_30_out | multiplexer_31_out | multiplexer_32_out | multiplexer_33_out | multiplexer_34_out | multiplexer_35_out | multiplexer_36_out | multiplexer_37_out | multiplexer_38_out | multiplexer_39_out | multiplexer_40_out;  // OR_Gate or_5, 7 bits wide
  Multiplexer #(.width(7), .enable("false")) multiplexer_41 (
    .in0({7{1'b0}}), .in1(7'b1111001), .out(multiplexer_41_out), .sel(add));
  Multiplexer #(.width(7), .enable("false")) multiplexer_42 (
    .in0({7{1'b0}}), .in1(7'b1111100), .out(multiplexer_42_out), .sel(sub));
  Multiplexer #(.width(7), .enable("false")) multiplexer_43 (
    .in0({7{1'b0}}), .in1(7'b1111001), .out(multiplexer_43_out), .sel(\and ));
  Multiplexer #(.width(7), .enable("false")) multiplexer_44 (
    .in0({7{1'b0}}), .in1(7'b0011000), .out(multiplexer_44_out), .sel(\or ));
  Multiplexer #(.width(7), .enable("false")) multiplexer_45 (
    .in0({7{1'b0}}), .in1(7'b0011000), .out(multiplexer_45_out), .sel(\nor ));
  Multiplexer #(.width(7), .enable("false")) multiplexer_46 (
    .in0({7{1'b0}}), .in1(7'b1111001), .out(multiplexer_46_out), .sel(I1));
  Multiplexer #(.width(7), .enable("false")) multiplexer_47 (
    .in0({7{1'b0}}), .in1(7'b0111100), .out(multiplexer_47_out), .sel(I2));
  Multiplexer #(.width(7), .enable("false")) multiplexer_48 (
    .in0({7{1'b0}}), .in1(7'b1000001), .out(multiplexer_48_out), .sel(addi));
  Multiplexer #(.width(7), .enable("false")) multiplexer_49 (
    .in0({7{1'b0}}), .in1(7'b1000001), .out(multiplexer_49_out), .sel(I4));
  Multiplexer #(.width(7), .enable("false")) multiplexer_50 (
    .in0({7{1'b0}}), .in1(7'b1001111), .out(multiplexer_50_out), .sel(beq));
  Multiplexer #(.width(7), .enable("false")) multiplexer_51 (
    .in0({7{1'b0}}), .in1(7'b0111100), .out(multiplexer_51_out), .sel(mult));
  Multiplexer #(.width(7), .enable("false")) multiplexer_52 (
    .in0({7{1'b0}}), .in1(7'b1100001), .out(multiplexer_52_out), .sel(JC));
  assign D3 = multiplexer_41_out | multiplexer_42_out | multiplexer_43_out | multiplexer_44_out | multiplexer_45_out | multiplexer_46_out | multiplexer_47_out | multiplexer_48_out | multiplexer_49_out | multiplexer_50_out | multiplexer_51_out | multiplexer_52_out;  // OR_Gate or_6, 7 bits wide

  assign J = {RS, RT, ADDRESS};

  // Other names for the same wires on the sheet: I3 = addi; I5 = beq; I = out_26; lw = I1; ori = I4; R = out_25;
  //   sw = I2

  // Notes on the sheet:
  //   rd
endmodule
